# Fritzing sketch Schema (saved by Fritzing 0.9.3b)
breadboards: 1

parts:
  Raspberry_Pi = Raspberry Pi 2
  IC1 = Voltage Regulator [package=to220-igo]
  U1 = LIPO-2000mAh [package=lipo-2000]
  U2 = LIPO-2000mAh [package=lipo-2000]
  J1 = Basic Servo
  LED1 = LED - 5mm [color="Green (565nm)" package="5 mm [THT]"]
  LED2 = LED - 5mm [color="Yellow (585nm)" package="5 mm [THT]"]
  U3 = L298 [package=multiwatt15]
  S1 = Round Pushbutton
  S2 = Round Pushbutton
  M1 = DC Motor
  M2 = DC Motor
  U4 = MLX90614 [package=to-39]
  U5 = MLX90614 [package=to-39]
  U6 = MLX90614 [package=to-39]
  U7 = MLX90614 [package=to-39]
  Componente1 = Adafruit TCS34725 RGB Color Sensor [part_number="Adafruit #1334"]
  Componente2 = Adafruit VL53L0X Time of Flight Distance Sensor [part_number="Adafruit #3317"]
  Componente3 = Adafruit VL53L0X Time of Flight Distance Sensor [part_number="Adafruit #3317"]
  Componente4 = Adafruit VL53L0X Time of Flight Distance Sensor [part_number="Adafruit #3317"]
  Componente5 = Adafruit VL53L0X Time of Flight Distance Sensor [part_number="Adafruit #3317"]
  Componente6 = 9-DOF Absolute Orientation IMU Fusion Breakout - BNO055
  Componente7 = Adafruit TCA9548A

nets:
  N1: Raspberry_Pi.GPIO2, Componente7.INPUTSDA
  N2: Raspberry_Pi.GPIO3, Componente7.INPUTSCL
  GND: Raspberry_Pi.GND, U2.-, J1.gnd, LED1.cathode, LED2.cathode, U3.GND, Componente2.GND, Componente3.GND, Componente4.GND, Componente5.GND, Componente6.GND
  N3: Raspberry_Pi.GPIO10, S2.leg1
  N4: Raspberry_Pi.GPIO9, S1.leg1
  N5: Raspberry_Pi.GPIO11, U3.IN1
  N6: Raspberry_Pi.GPIO5, U3.IN4
  N7: Raspberry_Pi.GPIO6, U3.IN3
  N8: Raspberry_Pi.GPIO13, U3.ENB
  N9: Raspberry_Pi.GPIO19, U3.ENA
  N10: Raspberry_Pi.GPIO26, U3.IN2
  N11: Raspberry_Pi.GPIO21, LED2.anode
  N12: Raspberry_Pi.GPIO20, LED1.anode
  N13: Raspberry_Pi.GPIO12, J1.pulse
  N14: Raspberry_Pi.GPIO18, Componente6.RST_5V
  N15: Raspberry_Pi.GPIO15, Componente6.SDA_5V
  N16: Raspberry_Pi.GPIO14, Componente6.SCL_5V
  VIN: Raspberry_Pi.5V, IC1.OUT, J1.vcc, U7.VDD, Componente2.VIN, Componente3.VIN, Componente4.VIN, Componente5.VIN, Componente6.5.0V
  N17: IC1.IN, U1.+, U3.VS
  N18: U3.OUT1, M1.pin_1
  N19: U3.OUT2, M1.pin_2
  N20: U3.OUT3, M2.pin_1
  N21: U3.OUT4, M2.pin_2
  VSS: S1.leg0, S2.leg0, U4.VSS, U5.VSS, U6.VSS, U7.VSS, Componente1.GND, Componente7.GND
  N22: U4.SCL_VZ, U5.SCL_VZ, U6.SCL_VZ, U7.SCL_VZ
  N23: U4.PWM_SDA, U5.PWM_SDA, U6.PWM_SDA, U7.PWM_SDA
  VDD: U4.VDD, U5.VDD, U6.VDD
  VIN_2: Componente1.VIN, Componente7.VCC
  N24: Componente1.SCL, Componente7.7SCL
  N25: Componente1.SDA, Componente7.7SDA
  N26: Componente2.SCL, Componente7.3SCL
  N27: Componente2.SDA, Componente7.3SDA
  N28: Componente3.SCL, Componente7.2SCL
  N29: Componente3.SDA, Componente7.2SDA
  N30: Componente4.SCL, Componente7.0SCL
  N31: Componente4.SDA, Componente7.0SDA
  N32: Componente5.SCL, Componente7.1SCL
  N33: Componente5.SDA, Componente7.1SDA

custom parts:
  Adafruit TCS34725 RGB Color Sensor: Your electronics can now see in dazzling color with this lovely color light sensor. We found the best color sensor on the market, the TCS34725, which has RGB and Clear light sensing elements. An IR blocking filter, integrated on-chip and localized to the color sensing photodiodes, minimizes the IR spectral component of the incoming light and allows color measurements to be made accurately. The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
  Adafruit VL53L0X Time of Flight Distance Sensor: The VL53L0X is a Time of Flight distance sensor like no other you've used! The sensor contains a very tiny invisible laser source, and a matching sensor. The VL53L0X can detect the "time of flight", or how long the light has taken to bounce back to the sensor. Since it uses a very narrow light source, it is good for determining distance of only the surface directly in front of it. Unlike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
  9-DOF Absolute Orientation IMU Fusion Breakout - BNO055: A MEMS accelerometer, magnetometer and gyroscope on a single die with a high speed ARM Cortex-M0 based processor to digest all the sensor data, abstract the sensor fusion and real time requirements away, and spit out data you can use in quaternions, Euler angles or vectors.
  Adafruit TCA9548A: You just found the perfect I2C sensor, and you want to wire up two or three or more of them to your Arduino when you realize "Uh oh, this chip has a fixed I2C address, and from what I know about I2C, you cannot have two devices with the same address on the same SDA/SCL pins!" Are you out of luck? You would be, if you didn't have this ultra-cool TCA9548A 1-to-8 I2C multiplexer! Finally, a way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
