# Fritzing sketch MLX90614-dx (saved by Fritzing 0.9.2b)
circuit board: 1.98691cm x 1.22293cm
breadboards: 1

parts:
  U1 = MLX90614 [package=to-39]
  U2 = mystery part, 4 pins [chip_label=?]
  R1 = Resistor [tolerance=±5% resistance=220 package=THT]
  R2 = Resistor [tolerance=±5% resistance=220 package=THT]

nets:
  N1: U1.SCL_VZ, U2.pin3, R1.Pin_1
  N2: U1.PWM_SDA, U2.pin4, R2.Pin_1
  N3: U1.VDD, U2.pin2, R1.Pin_0, R2.Pin_0
  N4: U1.VSS, U2.pin1
