# Fritzing sketch various board (saved by Fritzing 0.9.2b)
circuit board: 4.68007cm x 2.4365cm
breadboards: 1

parts:
  U1 = mystery part, 4 pins [chip_label=?]
  R1 = Resistor [tolerance=±5% resistance=220 package=THT]
  R2 = Resistor [tolerance=±5% resistance=220 package=THT]
  U2 = mystery part, 5 pins [chip_label=?]
  U3 = mystery part, 5 pins [chip_label=?]
  U4 = mystery part, 5 pins [chip_label=?]
  C1 = Electrolytic Capacitor [capacitance=1µF package="100 mil [THT, electrolytic]"]
  C2 = Electrolytic Capacitor [capacitance=1µF package="100 mil [THT, electrolytic]"]
  U5 = MLX90614 [package=to-39]
  U6 = mystery part, 4 pins [chip_label=?]
  R3 = Resistor [tolerance=±5% resistance=220 package=THT]
  R4 = Resistor [tolerance=±5% resistance=220 package=THT]
  U7 = MLX90614 [package=to-39]
  U8 = mystery part, 4 pins [chip_label=?]
  R5 = Resistor [tolerance=±5% resistance=220 package=THT]
  R6 = Resistor [tolerance=±5% resistance=220 package=THT]

nets:
  N1: U1.pin1, R1.Pin_1
  N2: U1.pin2, R1.Pin_0, R2.Pin_0
  N3: U1.pin3, U1.pin4, R2.Pin_1
  N4: U2.pin1, U2.pin2, U2.pin3, U2.pin4, U2.pin5, C2.+
  N5: U3.pin1, U3.pin2, U3.pin3, U3.pin4, U3.pin5, C1.+
  N6: U4.pin1, U4.pin2, U4.pin3, U4.pin4, U4.pin5, C1.-, C2.-
  N7: U5.SCL_VZ, U6.pin3, R3.Pin_1
  N8: U5.PWM_SDA, U6.pin4, R4.Pin_1
  N9: U5.VDD, U6.pin2, R3.Pin_0, R4.Pin_0
  N10: U5.VSS, U6.pin1
  N11: U7.SCL_VZ, U8.pin4, R6.Pin_1
  N12: U7.PWM_SDA, U8.pin3, R5.Pin_1
  N13: U7.VDD, U8.pin2, R5.Pin_0, R6.Pin_0
  N14: U7.VSS, U8.pin1
